# Fritzing sketch STM32与OpenMV (saved by Fritzing 0.9.3b)
breadboards: 1

parts:
  元件1 = BluePill
  U1 = OpenMV3

nets:
  N1: 元件1.B10, U1.P5/RX3/SDA
  N2: 元件1.B11, U1.P4/TX3/SCL
  GND3: 元件1.GND3, U1.GND
  5V: 元件1.5V, U1.VIN

custom parts:
  OpenMV3: OpenMV Cam
