# Fritzing sketch STM32与按键 (saved by Fritzing 0.9.3b)
breadboards: 1

parts:
  元件1 = BluePill
  Part1 = KY-004 Key Switch Module [package="Breakout board"]
  Part2 = KY-004 Key Switch Module [package="Breakout board"]
  Part3 = KY-004 Key Switch Module [package="Breakout board"]
  Part4 = KY-004 Key Switch Module [package="Breakout board"]

nets:
  N1: 元件1.GND3, Part1.-, Part2.-, Part3.-, Part4.-
  VIN: 元件1.5V, Part1.Vin, Part2.Vin, Part3.Vin, Part4.Vin
  N2: 元件1.B7, Part2.S
  N3: 元件1.B6, Part1.S
  N4: 元件1.B5, Part4.S
  N5: 元件1.B4, Part3.S

custom parts:
  KY-004 Key Switch Module: Arduino Key Switch Module Keyes KY-004 is a push button that will output a high signal when pressed.
